# Fritzing sketch sdcon_PCB (saved by Fritzing 0.9.3b)
circuit board: 4.55813cm x 3.90486cm
breadboards: 1

parts:
  J1 = female pin header, 12 pins [form="♀ (female)"]
  Start = female pin header, 4 pins [form="♀ (female)"]
  BT_B = female pin header, 4 pins [form="♀ (female)"]
  Enc_L = female pin header, 4 pins [form="♀ (female)"]
  Enc_R = female pin header, 4 pins [form="♀ (female)"]
  BT_A = female pin header, 4 pins [form="♀ (female)"]
  Extra = female pin header, 4 pins [form="♀ (female)"]  # not connected
  J2 = female pin header, 12 pins [form="♀ (female)"]
  BT_C = female pin header, 4 pins [form="♀ (female)"]
  FX_R = female pin header, 4 pins [form="♀ (female)"]
  FX_L = female pin header, 4 pins [form="♀ (female)"]
  BT_D = female pin header, 4 pins [form="♀ (female)"]

nets:
  N1: J1.pin1, Start.pin2
  N2: J1.pin2, BT_B.pin2
  N3: J1.pin3, BT_C.pin2
  N4: J1.pin4, BT_C.pin3
  N5: J1.pin5, BT_D.pin2
  N6: J1.pin6, FX_R.pin2
  N7: J1.pin7, FX_R.pin3
  N8: J1.pin8, FX_L.pin2
  N9: J1.pin9, Enc_L.pin1, Enc_R.pin1
  N10: Start.pin3, J2.pin1
  N11: BT_B.pin3, J2.pin2
  N12: Enc_L.pin3, J2.pin6
  N13: Enc_L.pin4, J2.pin7
  N14: Enc_R.pin3, J2.pin11
  N15: Enc_R.pin4, J2.pin12
  N16: BT_A.pin2, J2.pin3
  N17: BT_A.pin3, J2.pin4
  N18: J2.pin5, BT_D.pin3
  N19: J2.pin8, FX_L.pin3

notes:
  sdcon
  ProMicro
  SDCON
  NC-1
